# Fritzing sketch Sprint (saved by Fritzing 0.9.3b)
breadboards: 1

parts:
  Simulando_a_bateria_do_carro = Battery block 9V  # not connected
  VCC6 = Battery block 9V  # not connected
  VCC7 = Battery block 9V  # not connected
  Componente1 = Arduino Uno (Rev3) - ICSP
  Sensor_de_temperatura = TMP36 [package=to-92-kit]
  R1 = Resistor [tolerance=±5% resistance=0.1 package="1206 [SMD]"]
  Simulando_os_componentes_elétricos_do_carro = DC Motor  # not connected
  VCC9 = Battery block 9V
  Reed_Switch_Magnético = Reed switch [package=THT]
  R2 = Resistor [tolerance=±5% resistance=10k package="0603 [SMD]"]

nets:
  N1: Componente1.A0, Sensor_de_temperatura.VOUT
  N2: Componente1.A1, R1.Pin_0
  N3: Componente1.D2, Reed_Switch_Magnético.pin_2, R2.Pin_1
  5V: Componente1.5V, Sensor_de_temperatura.VCC, Reed_Switch_Magnético.pin_1
  N4: Componente1.GND, R1.Pin_1, VCC9.-
  N5: Sensor_de_temperatura.GND, R2.Pin_0

// code stored in the sketch: sprintCod.ino
const int pinShunt = A1;
const int pinTemp = A0;
const int pinIma = 2;
double Volts = 0;
float raioPneu = 22.86; // Raio em CM
float tempoDecorrido = 0, tempoInciaVel = 0, veloKm = 0;
// Valor da resistência do shunt em microohms
const float shuntResistance = 204*0.1; // Exemplo: 0.1 ohm

// Função para calcular a corrente com base na leitura do pino do shunt
float calcularWatts() {
  int shuntVoltage = analogRead(pinShunt);
  
  // Calcula a corrente usando a lei de Ohm: I = V / R
  float corrente = shuntVoltage / shuntResistance;
  return corrente * 5;
}

float tempCelsius(){
  double tempRead = analogRead(pinTemp);
  Volts = (tempRead / 1024.0) * 5000; // 5000 para obter em milivolts
  return (Volts-500) * 0.1; // temperatura em Celsius
}

float velocidade(){
	tempoDecorrido = millis() - tempoIniciaVel;
	float comprimento =  ((float) 2*3.1415*(raioPneu/100));
	tempoInciaVel = millis();
	veloKm = (3.6*comprimento)/tempoDecorrido;
	Serial.println("Velocidade: ");
	Serial.print(veloKm);
	Serial.println("KM/Hr");
	tempoZeraVel = velo;
}

void setup() {
  // Inicialização do monitor serial
  	Serial.begin(9600);
	tempoInciaVel = millis();
	attachInterrupt(digitalPinToInterrupt(2), velocidade, RISING);
}

void loop() {
  // Ler a corrente
  float watts = calcularWatts();
  float temperatura = tempCelsius();
  // Envia a corrente para o monitor serial
 	 Serial.print("Temperatura: ");
	Serial.print(temperatura,1);
	Serial.println("ºC");
	Serial.print("Uso da bateria: ");
	Serial.print(watts/1000);
	Serial.println("KW");
	if(millis() - tempoZeraVel > 5000){
		veloKm 0;
	}
	delay(1000):
}
